# Fritzing sketch circuit (saved by Fritzing 0.9.4)
circuit board: 15cm x 10cm
breadboards: 2

parts:
  IC2 = DIP - 40 pins [chip_label=W65C02 package="DIP (Dual Inline) [THT]"]
  Teensy1 = Teensy 3.6 (Basic)
  J1 = shrouded pin header, 10 pins [form="♂ (shrouded male)"]
  J1_2 = shrouded pin header, 10 pins [form="♂ (shrouded male)"]

nets:
  N1: IC2.RDY, Teensy1.D12
  N2: IC2.IRQB, Teensy1.D24
  N3: IC2.NMIB, Teensy1.D7
  VDD: IC2.VDD, IC2.BE, IC2.SOB, Teensy1.3V3, Teensy1.3V3_1
  N4: IC2.A0, Teensy1.A9/D23
  N5: IC2.A1, Teensy1.A8/D22
  N6: IC2.A2, Teensy1.A7/D21
  N7: IC2.A3, Teensy1.A6/D20
  N8: IC2.A4, Teensy1.A5/D19
  N9: IC2.A5, Teensy1.A4/D18
  N10: IC2.A6, Teensy1.A3/D17
  N11: IC2.A7, Teensy1.A2/D16
  N12: IC2.A8, Teensy1.A1/D15
  N13: IC2.A9, Teensy1.A0/D14
  N14: IC2.A10, Teensy1.D13
  N15: IC2.A11, Teensy1.D39
  VSS: IC2.VSS, Teensy1.GND, Teensy1.GND1, J1.pin1, J1_2.pin1
  N16: IC2.A12, Teensy1.D38
  N17: IC2.A13, Teensy1.D37
  N18: IC2.A14, Teensy1.D36
  N19: IC2.A15, Teensy1.D35
  N20: IC2.D7, Teensy1.D32
  N21: IC2.D6, Teensy1.D31
  N22: IC2.D5, Teensy1.D30
  N23: IC2.D4, Teensy1.D29
  N24: IC2.D3, Teensy1.D28
  N25: IC2.D2, Teensy1.D27
  N26: IC2.D1, Teensy1.D26
  N27: IC2.D0, Teensy1.D25
  N28: IC2.RWB, Teensy1.D34
  N29: IC2.PHI2, Teensy1.D8, Teensy1.D9
  N30: IC2.RESB, Teensy1.D33
  N31: Teensy1.D0, J1.pin10, J1_2.pin10
  N32: Teensy1.D1, J1.pin9, J1_2.pin9
  N33: Teensy1.D2, J1.pin8, J1_2.pin8
  N34: Teensy1.D3, J1.pin7, J1_2.pin7
  N35: Teensy1.D4, J1.pin6, J1_2.pin6
  N36: Teensy1.D5, J1.pin5, J1_2.pin5
  N37: Teensy1.D6, J1.pin4, J1_2.pin4
  N38: Teensy1.D10, J1.pin2, J1_2.pin2
  N39: Teensy1.D11, J1.pin3, J1_2.pin3

notes:
  6502 PC
  Eric Wimberley
  Rev. 1

custom parts:
  DIP - 40 pins: A DIP stand-in part for whatever IC you want. With 40 pins on a 300mil dual inline package (DIP) footprint.
  Teensy 3.6 (Basic): The Teensy is a complete USB-based microcontoller development system, in a very small footprint, capable of implementing many types of projects. All programming is done via the USB port. No special programmer is needed, only a standard micro-USB cable and a PC or Macintosh with a USB port.
